# Fritzing sketch Final_Project_Schematic (saved by Fritzing 0.9.4)
circuit board: 8.46667cm x 5.64444cm
breadboards: 3

parts:
  Part1 = Arduino Uno (Rev3)
  M1 = RioRand LM2596
  U1 = LIPO-2000mAh [package=lipo-2000]
  BAT1 = BC9VPC [package=bc9vpc]
  Part2 = InvenSense MPU6050
  Part5 = Bluetooth HC-05 Macho
  M2 = DC Motor
  M3 = DC Motor
  R1 = Resistor [tolerance=±5% resistance=1k package=THT]
  R2 = Resistor [tolerance=±5% resistance=2.2k package=THT]
  Part4 = Motor Driver 1A Dual TB6612FNG
  HC-SR04_Sensor_1 = HC-SR04 Ultrasonic Distance Sensor
  HC-SR04_Sensor_2 = HC-SR04 Ultrasonic Distance Sensor

nets:
  N1: Part1.A4/SDA, Part2.SDA
  N2: Part1.D8, Part4.BIN1
  N3: Part1.D9_PWM, Part4.STBY
  N4: Part1.D10_PWM/SS, HC-SR04_Sensor_2.ECHO
  N5: Part1.D11_PWM/MOSI, HC-SR04_Sensor_2.TRIG
  N6: Part1.D12/MISO, HC-SR04_Sensor_1.ECHO
  N7: Part1.D13/SCK, HC-SR04_Sensor_1.TRIG
  GND: Part1.GND, Part1.VIN, M1.Pin_4, BAT1.V+, BAT1.V-, Part2.GND, Part5.GND, R2.Pin_0, Part4.GND, HC-SR04_Sensor_1.GND, HC-SR04_Sensor_2.GND
  N8: Part1.A5/SCL, Part2.SCL
  N9: Part1.D0/RX, Part5.TXD
  N10: Part1.D1/TX, R1.Pin_1
  N11: Part1.D2, Part2.INT
  N12: Part1.D3_PWM, Part4.AIN1
  N13: Part1.D4, Part4.AIN2
  N14: Part1.D5_PWM, Part4.PWMA
  N15: Part1.D6_PWM, Part4.PWMB
  N16: Part1.D7, Part4.BIN2
  VCC: Part1.5V, Part2.VCC, Part5.VCC, Part4.VCC, HC-SR04_Sensor_1.VCC, HC-SR04_Sensor_2.VCC
  N17: M1.Pin_1, U1.+
  N18: M1.Pin_2, U1.-
  N19: M1.Pin_3, Part4.VM
  N20: Part5.RXD, R1.Pin_0, R2.Pin_1
  N21: M2.pin_1, Part4.A02
  N22: M2.pin_2, Part4.A01
  N23: M3.pin_1, Part4.B01
  N24: M3.pin_2, Part4.B02
