# Fritzing sketch Final_Project_Schematic_L298N (saved by Fritzing 0.9.4)
circuit board: 8.46667cm x 5.64444cm
breadboards: 2

parts:
  BAT1 = BC9VPC [package=bc9vpc]
  Gyro = InvenSense MPU6050
  Bluetooth_Transmitter = Bluetooth HC-05 Macho
  M2 = DC Motor
  M3 = DC Motor
  R1 = Resistor [tolerance=±5% resistance=1k package=THT]
  R2 = Resistor [tolerance=±5% resistance=2.2k package=THT]
  US_Sensor_1 = HC-SR04 Ultrasonic Distance Sensor
  US_Sensor_2 = HC-SR04 Ultrasonic Distance Sensor
  Arduino = Arduino Uno (Rev3)
  R3 = Resistor [tolerance=±5% resistance=220 package=THT]
  LED1 = LED - 5mm [color="Blue (470nm)" package="5 mm [THT]"]
  VCC1 = Battery block 9V
  Motor_Driver = L298N DC motor driver

nets:
  N1: BAT1.V+, Arduino.VIN
  GND: BAT1.V-, Gyro.GND, Bluetooth_Transmitter.GND, R2.Pin_0, US_Sensor_1.GND, US_Sensor_2.GND, Arduino.GND, LED1.cathode, VCC1.-, Motor_Driver.GND
  VCC: Gyro.VCC, Bluetooth_Transmitter.VCC, US_Sensor_1.VCC, US_Sensor_2.VCC, Arduino.5V
  N2: Gyro.SCL, Arduino.A5/SCL
  N3: Gyro.SDA, Arduino.A4/SDA
  N4: Gyro.INT, Arduino.D2
  N5: Bluetooth_Transmitter.TXD, Arduino.D0/RX
  N6: Bluetooth_Transmitter.RXD, R1.Pin_0, R2.Pin_1
  N7: M2.pin_1, Motor_Driver.OUT2
  N8: M2.pin_2, Motor_Driver.OUT1
  N9: M3.pin_1, Motor_Driver.OUT3
  N10: M3.pin_2, Motor_Driver.OUT4
  N11: R1.Pin_1, Arduino.D1/TX
  N12: US_Sensor_1.TRIG, Arduino.D13/SCK
  N13: US_Sensor_1.ECHO, Arduino.D12/MISO
  N14: US_Sensor_2.TRIG, Arduino.D11_PWM/MOSI
  N15: US_Sensor_2.ECHO, Arduino.D10_PWM/SS
  N16: Arduino.D8, Motor_Driver.IN3
  N17: Arduino.D9_PWM, R3.Pin_1
  N18: Arduino.D3_PWM, Motor_Driver.IN1
  N19: Arduino.D4, Motor_Driver.IN2
  N20: Arduino.D5_PWM, Motor_Driver.ENA
  N21: Arduino.D6_PWM, Motor_Driver.IN4
  N22: Arduino.D7, Motor_Driver.ENB
  N23: R3.Pin_0, LED1.anode
  N24: VCC1.+, Motor_Driver.12V, Motor_Driver.5V-ENA-JMP-I, Motor_Driver.5V-ENA-JMP-O

notes:
  JST Balancing Robot, Balancing robot circut with US sensors., 1

custom parts:
  L298N DC motor driver: 2x DC motor driver with 78M05 positive voltage regulator (7..35 V) L298N: max 46 V, 2 A Set 5 V Enable jumper to enable 5 V regultor (needed for the L298N) and +5 V output at screw terminal or supply external +5 V at screw terminal Set ENA and/or ENB to +5 V to enable motor permanently or supply ENA and/or ENB with PWM signal IN1 and IN2 set rotation directory for motor A (OUT1/OUT2) IN2 and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
